# Fritzing sketch main (saved by Fritzing 0.9.10b)

parts:
  arduino = Arduino Nano (Rev3.0)
  bt = Bluetooth HC-06u [package=THT]
  F1 = Fan - 4 wire [package=THT]
  5V_->_12V = Boost Convertor [part_number=XL6009E1 package=THT]
  water_pump = water pump/motor
  R1 = Resistor [tolerance=±5% resistance=100 package="0805 [SMD]"]
  R2 = Resistor [tolerance=±5% resistance=100 package="0805 [SMD]"]
  R3 = Resistor [tolerance=±5% resistance=100 package="0805 [SMD]"]
  LED1 = smd LED [color="Red (633nm)" package="1206 [SMD]"]

nets:
  GND: arduino.GND, bt.GND, 5V_->_12V.Negative_Input, LED1.cathode
  N1: arduino.D5, F1.PWM
  N2: arduino.D7, bt.TXD
  N3: arduino.D8, bt.RXD
  5V: arduino.5V, bt.VCC, 5V_->_12V.Positive_Input, R1.Pin_0
  N4: arduino.A0, F1.Tach
  N5: F1.GND, 5V_->_12V.Negative_Output, water_pump.pin_2
  N6: F1.Power, 5V_->_12V.Positive_Output, water_pump.pin_1
  N7: R1.Pin_1, R3.Pin_0
  N8: R2.Pin_0, R3.Pin_1
  N9: R2.Pin_1, LED1.anode

custom parts:
  Bluetooth HC-06u: Bluetooth HC-06 - face up, pins down 16.5mm x 37.5mm PCB
  Fan - 4 wire: Fan, 4 wire with tach.
  Boost Convertor: DC to DC boost convertor
  water pump/motor: WATER PUMP BY ARDUBLOCKTR
